# Fritzing sketch LINK_01 (saved by Fritzing 0.9.6b)
breadboards: 3

parts:
  C1 = Ceramic Capacitor [capacitance="100 nF" voltage=35V package="0603 [SMD, multilayer]"]
  Mod1 = Raspberry Pi Pico
  Mod2 = Raspberry Pi 4B
  R2 = Resistor [tolerance=±5% power=0.25 resistance=47 package=THT]
  R3 = Resistor [tolerance=±5% power=0.25 resistance=47 package=THT]
  R4 = Resistor [tolerance=±5% power=0.25 resistance=47 package=THT]
  R5 = Resistor [tolerance=±5% power=0.25 resistance=47 package=THT]
  R6 = Resistor [tolerance=±5% power=0.25 resistance=47 package=THT]
  R7 = Resistor [tolerance=±5% power=0.25 resistance=220 package=THT]
  R8 = Resistor [tolerance=±5% power=0.25 resistance=220 package=THT]
  R9 = Resistor [tolerance=±5% power=0.25 resistance=220 package=THT]
  R10 = Resistor [tolerance=±5% power=0.25 resistance=220 package=THT]
  R11 = Resistor [tolerance=±5% power=0.25 resistance=220 package=THT]

nets:
  N1: C1.1, Mod1.pin_3, Mod1.pin_33, Mod1.pin_42, Mod2.GND
  N2: Mod1.pin_41, Mod2.GPIO25
  N3: Mod1.pin_43, Mod2.GPIO24
  N4: R2.Pin_1, R9.Pin_1
  N5: R3.Pin_1, R10.Pin_1
  N6: R4.Pin_1, R11.Pin_1
  N7: R5.Pin_1, R8.Pin_1
  N8: R6.Pin_1, R7.Pin_1

custom parts:
  Raspberry Pi Pico: Raspberry Pi Pico. Based around the RP2040 microcontroller the Pico is a low cost microcontroller device bringing Raspberry Pi quality, cost, and easy of use to the microcontroller space. Jan 2021, Split part in to two versions: tht (this one) and SMD. This one will drill holes for a .1 in header in pcb to allow plugging in the module as well as providing pads to solder the module to the top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
