// Logisim project LINK_01.circ as structural Verilog
module main (
);

  ROM #(.addrWidth(13)) rom_1 ();  // open: addr, data
  RAM #(.addrWidth(15)) ram_1 ();  // open: addr, we, oe, clk, din, dout
endmodule
